# Fritzing sketch Arduino Radar (saved by Fritzing 0.9.3b)
breadboards: 2

parts:
  Part1 = Arduino Uno (Rev3)
  YwRobot_Power_Supply1 = YwRobot Breadboard Power Supply [part_number=545043]
  HC-SR04_Sensor_1 = HC-SR04 Ultrasonic Distance Sensor
  J1 = Basic Servo
  C1 = Electrolytic Capacitor [capacitance=100μF package="0807 [SMD, electrolytic]"]
  C2 = Electrolytic Capacitor [capacitance=0.1µF package="0807 [SMD, electrolytic]"]

nets:
  N1: Part1.D8, HC-SR04_Sensor_1.TRIG
  GND: Part1.GND, YwRobot_Power_Supply1.GND#13, YwRobot_Power_Supply1.GND#14, HC-SR04_Sensor_1.GND, J1.gnd, C1.-, C2.-
  N2: Part1.D3_PWM, J1.pulse, C2.+
  N3: Part1.D7, HC-SR04_Sensor_1.ECHO
  5V: Part1.5V, HC-SR04_Sensor_1.VCC
  N4: YwRobot_Power_Supply1.VCC#5, YwRobot_Power_Supply1.VCC#6
  N5: YwRobot_Power_Supply1.VCC#9, YwRobot_Power_Supply1.VCC#10, J1.vcc, C1.+
  N6: YwRobot_Power_Supply1.GND#11, YwRobot_Power_Supply1.GND#12

custom parts:
  YwRobot Breadboard Power Supply: The YwRobot Breadboard Power Supply (MB-V2) has two power rails; they can be 5V or 3V3. Power to the module can be provided through the female USB socket or through the A10 (female) 2.1mm power jack.
  HC-SR04 Ultrasonic Distance Sensor: The HC-SR04 is an ultrasonic distance sensor. It is capable of providing measurement for ranges of 2cm to 400cm. The module operates at 5V.
